// Digital circuit MatrixControllerTest.dig as structural Verilog
module MatrixControllerTest (
  input  Clock,
  input  Reset,
  input  Show_Display,
  input  Desce_jogada,
  input  [5:0] Pontos,
  input  [2:0] Linhas_bloq,
  input  [3:0] Prox_jogada,
  input  Clock_display,
  input  clk,
  input  clk_2,
  input  clk_3,
  input  clk_4,
  input  clk_5,
  input  clk_6,
  input  clk_7,
  input  clk_8,
  input  clk_9,
  input  clk_10,
  input  clk_11,
  input  clk_12,
  input  clk_13,
  input  clk_14,
  input  clk_15,
  input  clk_16
);

  wire [3:0] register_4_q, register_5_q, register_6_q, register_10_q, register_11_q, register_12_q,
       register_16_q, register_17_q, register_18_q, register_22_q, register_23_q, register_24_q,
       register_28_q, register_29_q, register_30_q, register_34_q, register_35_q, register_36_q,
       register_40_q, register_41_q, register_42_q, register_46_q, register_47_q, register_48_q;
  wire [7:0] not_1_out, not_2_out, not_3_out, register_1_q, register_2_q, register_3_q, register_7_q,
       register_8_q, register_9_q, register_13_q, register_14_q, register_15_q, register_19_q, register_20_q,
       register_21_q, register_25_q, register_26_q, register_27_q, register_31_q, register_32_q,
       register_33_q, register_37_q, register_38_q, register_39_q, register_43_q, register_44_q,
       register_45_q, u_matrix_controller_matriz_b, u_matrix_controller_matriz_col,
       u_matrix_controller_matriz_g, u_matrix_controller_matriz_r;

  matrix_controller #(.applicationType("IVERILOG")) u_matrix_controller (
    .clock(Clock), .display_refresh_clock(Clock_display), .reset_display(Reset), .show_display(Show_Display),
    .desce_jogada(Desce_jogada), .pontos(Pontos), .linhas_bloqueadas(Linhas_bloq), .prox_jogada(Prox_jogada),
    .matriz_col(u_matrix_controller_matriz_col), .matriz_r(u_matrix_controller_matriz_r),
    .matriz_g(u_matrix_controller_matriz_g), .matriz_b(u_matrix_controller_matriz_b));
  assign not_1_out = ~u_matrix_controller_matriz_r;  // Not not_1, 8 bits wide
  assign not_2_out = ~u_matrix_controller_matriz_b;  // Not not_2, 8 bits wide
  assign not_3_out = ~u_matrix_controller_matriz_g;  // Not not_3, 8 bits wide
  Register #(.Bits(8)) register_1 (.D(not_1_out), .C(clk_4), .en(u_matrix_controller_matriz_col[0]), .Q(register_1_q));
  Register #(.Bits(8)) register_2 (.D(not_3_out), .C(clk_4), .en(u_matrix_controller_matriz_col[0]), .Q(register_2_q));
  Register #(.Bits(8)) register_3 (.D(not_2_out), .C(clk_4), .en(u_matrix_controller_matriz_col[0]), .Q(register_3_q));
  Register #(.Bits(4)) register_4 (
    .D(not_2_out[7:4]), .C(clk), .en(u_matrix_controller_matriz_col[0]), .Q(register_4_q));
  Register #(.Bits(4)) register_5 (
    .D(not_3_out[7:4]), .C(clk), .en(u_matrix_controller_matriz_col[0]), .Q(register_5_q));
  Register #(.Bits(4)) register_6 (
    .D(not_1_out[7:4]), .C(clk), .en(u_matrix_controller_matriz_col[0]), .Q(register_6_q));
  // RGBLED rgbled_1: pin names not known; wires that end beside it: register_1_q[0], register_2_q[0], register_3_q[0]
  // RGBLED rgbled_2: pin names not known; wires that end beside it: register_1_q[1], register_2_q[1], register_3_q[1]
  // RGBLED rgbled_3: pin names not known; wires that end beside it: register_1_q[2], register_2_q[2], register_3_q[2]
  // RGBLED rgbled_4: pin names not known; wires that end beside it: register_1_q[3], register_2_q[3], register_3_q[3]
  // RGBLED rgbled_5: pin names not known; wires that end beside it: register_6_q[0], register_5_q[0], register_4_q[0]
  // RGBLED rgbled_6: pin names not known; wires that end beside it: register_6_q[1], register_5_q[1], register_4_q[1]
  // RGBLED rgbled_7: pin names not known; wires that end beside it: register_6_q[2], register_5_q[2], register_4_q[2]
  // RGBLED rgbled_8: pin names not known; wires that end beside it: register_6_q[3], register_5_q[3], register_4_q[3]
  Register #(.Bits(8)) register_7 (.D(not_1_out), .C(clk_2), .en(u_matrix_controller_matriz_col[1]), .Q(register_7_q));
  Register #(.Bits(8)) register_8 (.D(not_3_out), .C(clk_2), .en(u_matrix_controller_matriz_col[1]), .Q(register_8_q));
  Register #(.Bits(8)) register_9 (.D(not_2_out), .C(clk_2), .en(u_matrix_controller_matriz_col[1]), .Q(register_9_q));
  Register #(.Bits(4)) register_10 (
    .D(not_2_out[7:4]), .C(clk_3), .en(u_matrix_controller_matriz_col[1]), .Q(register_10_q));
  Register #(.Bits(4)) register_11 (
    .D(not_3_out[7:4]), .C(clk_3), .en(u_matrix_controller_matriz_col[1]), .Q(register_11_q));
  Register #(.Bits(4)) register_12 (
    .D(not_1_out[7:4]), .C(clk_3), .en(u_matrix_controller_matriz_col[1]), .Q(register_12_q));
  // RGBLED rgbled_9: pin names not known; wires that end beside it: register_7_q[0], register_8_q[0], register_9_q[0]
  // RGBLED rgbled_10: pin names not known; wires that end beside it: register_7_q[1], register_8_q[1], register_9_q[1]
  // RGBLED rgbled_11: pin names not known; wires that end beside it: register_7_q[2], register_8_q[2], register_9_q[2]
  // RGBLED rgbled_12: pin names not known; wires that end beside it: register_7_q[3], register_8_q[3], register_9_q[3]
  // RGBLED rgbled_13: pin names not known; wires that end beside it: register_12_q[0], register_11_q[0], register_10_q[0]
  // RGBLED rgbled_14: pin names not known; wires that end beside it: register_12_q[1], register_11_q[1], register_10_q[1]
  // RGBLED rgbled_15: pin names not known; wires that end beside it: register_12_q[2], register_11_q[2], register_10_q[2]
  // RGBLED rgbled_16: pin names not known; wires that end beside it: register_12_q[3], register_11_q[3], register_10_q[3]
  Register #(.Bits(8)) register_13 (
    .D(not_1_out), .C(clk_8), .en(u_matrix_controller_matriz_col[2]), .Q(register_13_q));
  Register #(.Bits(8)) register_14 (
    .D(not_3_out), .C(clk_8), .en(u_matrix_controller_matriz_col[2]), .Q(register_14_q));
  Register #(.Bits(8)) register_15 (
    .D(not_2_out), .C(clk_8), .en(u_matrix_controller_matriz_col[2]), .Q(register_15_q));
  Register #(.Bits(4)) register_16 (
    .D(not_2_out[7:4]), .C(clk_5), .en(u_matrix_controller_matriz_col[2]), .Q(register_16_q));
  Register #(.Bits(4)) register_17 (
    .D(not_3_out[7:4]), .C(clk_5), .en(u_matrix_controller_matriz_col[2]), .Q(register_17_q));
  Register #(.Bits(4)) register_18 (
    .D(not_1_out[7:4]), .C(clk_5), .en(u_matrix_controller_matriz_col[2]), .Q(register_18_q));
  // RGBLED rgbled_17: pin names not known; wires that end beside it: register_13_q[0], register_14_q[0], register_15_q[0]
  // RGBLED rgbled_18: pin names not known; wires that end beside it: register_13_q[1], register_14_q[1], register_15_q[1]
  // RGBLED rgbled_19: pin names not known; wires that end beside it: register_13_q[2], register_14_q[2], register_15_q[2]
  // RGBLED rgbled_20: pin names not known; wires that end beside it: register_13_q[3], register_14_q[3], register_15_q[3]
  // RGBLED rgbled_21: pin names not known; wires that end beside it: register_18_q[0], register_17_q[0], register_16_q[0]
  // RGBLED rgbled_22: pin names not known; wires that end beside it: register_18_q[1], register_17_q[1], register_16_q[1]
  // RGBLED rgbled_23: pin names not known; wires that end beside it: register_18_q[2], register_17_q[2], register_16_q[2]
  // RGBLED rgbled_24: pin names not known; wires that end beside it: register_18_q[3], register_17_q[3], register_16_q[3]
  Register #(.Bits(8)) register_19 (
    .D(not_1_out), .C(clk_6), .en(u_matrix_controller_matriz_col[3]), .Q(register_19_q));
  Register #(.Bits(8)) register_20 (
    .D(not_3_out), .C(clk_6), .en(u_matrix_controller_matriz_col[3]), .Q(register_20_q));
  Register #(.Bits(8)) register_21 (
    .D(not_2_out), .C(clk_6), .en(u_matrix_controller_matriz_col[3]), .Q(register_21_q));
  Register #(.Bits(4)) register_22 (
    .D(not_2_out[7:4]), .C(clk_7), .en(u_matrix_controller_matriz_col[3]), .Q(register_22_q));
  Register #(.Bits(4)) register_23 (
    .D(not_3_out[7:4]), .C(clk_7), .en(u_matrix_controller_matriz_col[3]), .Q(register_23_q));
  Register #(.Bits(4)) register_24 (
    .D(not_1_out[7:4]), .C(clk_7), .en(u_matrix_controller_matriz_col[3]), .Q(register_24_q));
  // RGBLED rgbled_25: pin names not known; wires that end beside it: register_19_q[0], register_20_q[0], register_21_q[0]
  // RGBLED rgbled_26: pin names not known; wires that end beside it: register_19_q[1], register_20_q[1], register_21_q[1]
  // RGBLED rgbled_27: pin names not known; wires that end beside it: register_19_q[2], register_20_q[2], register_21_q[2]
  // RGBLED rgbled_28: pin names not known; wires that end beside it: register_19_q[3], register_20_q[3], register_21_q[3]
  // RGBLED rgbled_29: pin names not known; wires that end beside it: register_24_q[0], register_23_q[0], register_22_q[0]
  // RGBLED rgbled_30: pin names not known; wires that end beside it: register_24_q[1], register_23_q[1], register_22_q[1]
  // RGBLED rgbled_31: pin names not known; wires that end beside it: register_24_q[2], register_23_q[2], register_22_q[2]
  // RGBLED rgbled_32: pin names not known; wires that end beside it: register_24_q[3], register_23_q[3], register_22_q[3]
  Register #(.Bits(8)) register_25 (
    .D(not_1_out), .C(clk_12), .en(u_matrix_controller_matriz_col[4]), .Q(register_25_q));
  Register #(.Bits(8)) register_26 (
    .D(not_3_out), .C(clk_12), .en(u_matrix_controller_matriz_col[4]), .Q(register_26_q));
  Register #(.Bits(8)) register_27 (
    .D(not_2_out), .C(clk_12), .en(u_matrix_controller_matriz_col[4]), .Q(register_27_q));
  Register #(.Bits(4)) register_28 (
    .D(not_2_out[7:4]), .C(clk_9), .en(u_matrix_controller_matriz_col[4]), .Q(register_28_q));
  Register #(.Bits(4)) register_29 (
    .D(not_3_out[7:4]), .C(clk_9), .en(u_matrix_controller_matriz_col[4]), .Q(register_29_q));
  Register #(.Bits(4)) register_30 (
    .D(not_1_out[7:4]), .C(clk_9), .en(u_matrix_controller_matriz_col[4]), .Q(register_30_q));
  // RGBLED rgbled_33: pin names not known; wires that end beside it: register_25_q[0], register_26_q[0], register_27_q[0]
  // RGBLED rgbled_34: pin names not known; wires that end beside it: register_25_q[1], register_26_q[1], register_27_q[1]
  // RGBLED rgbled_35: pin names not known; wires that end beside it: register_25_q[2], register_26_q[2], register_27_q[2]
  // RGBLED rgbled_36: pin names not known; wires that end beside it: register_25_q[3], register_26_q[3], register_27_q[3]
  // RGBLED rgbled_37: pin names not known; wires that end beside it: register_30_q[0], register_29_q[0], register_28_q[0]
  // RGBLED rgbled_38: pin names not known; wires that end beside it: register_30_q[1], register_29_q[1], register_28_q[1]
  // RGBLED rgbled_39: pin names not known; wires that end beside it: register_30_q[2], register_29_q[2], register_28_q[2]
  // RGBLED rgbled_40: pin names not known; wires that end beside it: register_30_q[3], register_29_q[3], register_28_q[3]
  Register #(.Bits(8)) register_31 (
    .D(not_1_out), .C(clk_10), .en(u_matrix_controller_matriz_col[5]), .Q(register_31_q));
  Register #(.Bits(8)) register_32 (
    .D(not_3_out), .C(clk_10), .en(u_matrix_controller_matriz_col[5]), .Q(register_32_q));
  Register #(.Bits(8)) register_33 (
    .D(not_2_out), .C(clk_10), .en(u_matrix_controller_matriz_col[5]), .Q(register_33_q));
  Register #(.Bits(4)) register_34 (
    .D(not_2_out[7:4]), .C(clk_11), .en(u_matrix_controller_matriz_col[5]), .Q(register_34_q));
  Register #(.Bits(4)) register_35 (
    .D(not_3_out[7:4]), .C(clk_11), .en(u_matrix_controller_matriz_col[5]), .Q(register_35_q));
  Register #(.Bits(4)) register_36 (
    .D(not_1_out[7:4]), .C(clk_11), .en(u_matrix_controller_matriz_col[5]), .Q(register_36_q));
  // RGBLED rgbled_41: pin names not known; wires that end beside it: register_31_q[0], register_32_q[0], register_33_q[0]
  // RGBLED rgbled_42: pin names not known; wires that end beside it: register_31_q[1], register_32_q[1], register_33_q[1]
  // RGBLED rgbled_43: pin names not known; wires that end beside it: register_31_q[2], register_32_q[2], register_33_q[2]
  // RGBLED rgbled_44: pin names not known; wires that end beside it: register_31_q[3], register_32_q[3], register_33_q[3]
  // RGBLED rgbled_45: pin names not known; wires that end beside it: register_36_q[0], register_35_q[0], register_34_q[0]
  // RGBLED rgbled_46: pin names not known; wires that end beside it: register_36_q[1], register_35_q[1], register_34_q[1]
  // RGBLED rgbled_47: pin names not known; wires that end beside it: register_36_q[2], register_35_q[2], register_34_q[2]
  // RGBLED rgbled_48: pin names not known; wires that end beside it: register_36_q[3], register_35_q[3], register_34_q[3]
  Register #(.Bits(8)) register_37 (
    .D(not_1_out), .C(clk_16), .en(u_matrix_controller_matriz_col[6]), .Q(register_37_q));
  Register #(.Bits(8)) register_38 (
    .D(not_3_out), .C(clk_16), .en(u_matrix_controller_matriz_col[6]), .Q(register_38_q));
  Register #(.Bits(8)) register_39 (
    .D(not_2_out), .C(clk_16), .en(u_matrix_controller_matriz_col[6]), .Q(register_39_q));
  Register #(.Bits(4)) register_40 (
    .D(not_2_out[7:4]), .C(clk_13), .en(u_matrix_controller_matriz_col[6]), .Q(register_40_q));
  Register #(.Bits(4)) register_41 (
    .D(not_3_out[7:4]), .C(clk_13), .en(u_matrix_controller_matriz_col[6]), .Q(register_41_q));
  Register #(.Bits(4)) register_42 (
    .D(not_1_out[7:4]), .C(clk_13), .en(u_matrix_controller_matriz_col[6]), .Q(register_42_q));
  // RGBLED rgbled_49: pin names not known; wires that end beside it: register_37_q[0], register_38_q[0], register_39_q[0]
  // RGBLED rgbled_50: pin names not known; wires that end beside it: register_37_q[1], register_38_q[1], register_39_q[1]
  // RGBLED rgbled_51: pin names not known; wires that end beside it: register_37_q[2], register_38_q[2], register_39_q[2]
  // RGBLED rgbled_52: pin names not known; wires that end beside it: register_37_q[3], register_38_q[3], register_39_q[3]
  // RGBLED rgbled_53: pin names not known; wires that end beside it: register_42_q[0], register_41_q[0], register_40_q[0]
  // RGBLED rgbled_54: pin names not known; wires that end beside it: register_42_q[1], register_41_q[1], register_40_q[1]
  // RGBLED rgbled_55: pin names not known; wires that end beside it: register_42_q[2], register_41_q[2], register_40_q[2]
  // RGBLED rgbled_56: pin names not known; wires that end beside it: register_42_q[3], register_41_q[3], register_40_q[3]
  Register #(.Bits(8)) register_43 (
    .D(not_1_out), .C(clk_14), .en(u_matrix_controller_matriz_col[7]), .Q(register_43_q));
  Register #(.Bits(8)) register_44 (
    .D(not_3_out), .C(clk_14), .en(u_matrix_controller_matriz_col[7]), .Q(register_44_q));
  Register #(.Bits(8)) register_45 (
    .D(not_2_out), .C(clk_14), .en(u_matrix_controller_matriz_col[7]), .Q(register_45_q));
  Register #(.Bits(4)) register_46 (
    .D(not_2_out[7:4]), .C(clk_15), .en(u_matrix_controller_matriz_col[7]), .Q(register_46_q));
  Register #(.Bits(4)) register_47 (
    .D(not_3_out[7:4]), .C(clk_15), .en(u_matrix_controller_matriz_col[7]), .Q(register_47_q));
  Register #(.Bits(4)) register_48 (
    .D(not_1_out[7:4]), .C(clk_15), .en(u_matrix_controller_matriz_col[7]), .Q(register_48_q));
  // RGBLED rgbled_57: pin names not known; wires that end beside it: register_43_q[0], register_44_q[0], register_45_q[0]
  // RGBLED rgbled_58: pin names not known; wires that end beside it: register_43_q[1], register_44_q[1], register_45_q[1]
  // RGBLED rgbled_59: pin names not known; wires that end beside it: register_43_q[2], register_44_q[2], register_45_q[2]
  // RGBLED rgbled_60: pin names not known; wires that end beside it: register_43_q[3], register_44_q[3], register_45_q[3]
  // RGBLED rgbled_61: pin names not known; wires that end beside it: register_48_q[0], register_47_q[0], register_46_q[0]
  // RGBLED rgbled_62: pin names not known; wires that end beside it: register_48_q[1], register_47_q[1], register_46_q[1]
  // RGBLED rgbled_63: pin names not known; wires that end beside it: register_48_q[2], register_47_q[2], register_46_q[2]
  // RGBLED rgbled_64: pin names not known; wires that end beside it: register_48_q[3], register_47_q[3], register_46_q[3]

  // Notes on the sheet:
  //   Clock: Hz: 5
  //   Clock_display: Hz: 50
  //   clk: Hz: 100
  //   clk_2: Hz: 100
  //   clk_3: Hz: 100
  //   clk_4: Hz: 100
  //   clk_5: Hz: 100
  //   clk_6: Hz: 100
  //   clk_7: Hz: 100
  //   clk_8: Hz: 100
  //   clk_9: Hz: 100
  //   clk_10: Hz: 100
  //   clk_11: Hz: 100
  //   clk_12: Hz: 100
  //   clk_13: Hz: 100
  //   clk_14: Hz: 100
  //   clk_15: Hz: 100
  //   clk_16: Hz: 100
endmodule

/* Code of matrix_controller:
module matrix_controller (
	input clock, display_refresh_clock, reset_display, show_display, desce_jogada,
	
	input [5:0] pontos,
	input [2:0] linhas_bloqueadas,
	input	[3:0] prox_jogada,
	
	output reg [7:0] matriz_col, matriz_r, matriz_g, matriz_b

);

	//  LINHAS					COLUNA RGB	**ATIVO BAIXO**
	reg [7:0] display_buffer [7:0][2:0];
	
	reg [7:0] jogadas [3:0];
	
	
	wire [7:0] line_block_mask;
	
	assign line_block_mask = ~(8'b11111111 >> linhas_bloqueadas);
	
	always @(posedge clock) begin
		if (reset_display) begin
			jogadas[0] <= 8'b11111111;
			jogadas[1] <= 8'b11111111;
			jogadas[2] <= 8'b11111111;
			jogadas[3] <= 8'b11111111;
			
			display_buffer[0][0] <= 8'b11111111;
			display_buffer[0][1] <= 8'b11111111;
			display_buffer[0][2] <= 8'b11111111;
			
			display_buffer[1][0] <= 8'b11111111;
			display_buffer[1][1] <= 8'b11111111;
			display_buffer[1][2] <= 8'b11111111;
			
			display_buffer[2][0] <= 8'b11111111;
			display_buffer[2][1] <= 8'b11111111;
			display_buffer[2][2] <= 8'b11111111;
			
			display_buffer[3][0] <= 8'b11111111;
			display_buffer[3][1] <= 8'b11111111;
			display_buffer[3][2] <= 8'b11111111;
			
			display_buffer[4][0] <= 8'b11111111;
			display_buffer[4][1] <= 8'b11111111;
			display_buffer[4][2] <= 8'b11111111;
			
			display_buffer[5][0] <= 8'b11111111;
			display_buffer[5][1] <= 8'b11111111;
			display_buffer[5][2] <= 8'b11111111;
			
			display_buffer[6][0] <= 8'b11111111;
			display_buffer[6][1] <= 8'b11111111;
			display_buffer[6][2] <= 8'b11111111;
			
			display_buffer[7][0] <= 8'b11111111;
			display_buffer[7][1] <= 8'b11111111;
			display_buffer[7][2] <= 8'b11111111;
		end
		else begin
			
			if (desce_jogada) begin
				jogadas[0] <= {jogadas[0][6:0], ~prox_jogada[0]};
				jogadas[1] <= {jogadas[1][6:0], ~prox_jogada[1]};
				jogadas[2] <= {jogadas[2][6:0], ~prox_jogada[2]};
				jogadas[3] <= {jogadas[3][6:0], ~prox_jogada[3]};
			end
			
			display_buffer[2][0] <= jogadas[0] | line_block_mask;
			display_buffer[2][1] <= 8'b11111111 & (~line_block_mask);
			display_buffer[2][2] <= 8'b11111111 & (~line_block_mask);
			
			display_buffer[3][0] <= 8'b11111111;
			display_buffer[3][1] <= (jogadas[1] | line_block_mask) & (~line_block_mask);
			display_buffer[3][2] <= 8'b11111111 & (~line_block_mask);
			
			display_buffer[4][0] <= 8'b11111111;
			display_buffer[4][1] <= 8'b11111111 & (~line_block_mask);
			display_buffer[4][2] <= (jogadas[2] | line_block_mask) & (~line_block_mask);
			
			display_buffer[5][0] <= jogadas[3] | line_block_mask;
			display_buffer[5][1] <= (jogadas[3] | line_block_mask) & (~line_block_mask);
			display_buffer[5][2] <= 8'b11111111 & (~line_block_mask);
			
			
			
			{display_buffer[0][0], display_buffer[1][0], display_buffer[6][0], display_buffer[7][0]} <= 32'hFFFFFFFF >> pontos;
			{display_buffer[0][2], display_buffer[1][2], display_buffer[6][2], display_buffer[7][2]} <= 32'hFFFFFFFF >> pontos;
		
		end
	end
	
	
	wire [2:0] selected_col;
	
	contador_m #(.M(8), .N(3)) col_selector (
		.clock(display_refresh_clock),
		.zera_as(reset_display),
		.zera_s(1'b0),
		.conta(show_display),
		.Q(selected_col),
		.fim(),
		.meio()
	);
	
	always @(selected_col) begin
	
		case (selected_col) 
			3'b000: begin
				matriz_col 	<= 8'b00000001;
				matriz_r 	<= display_buffer[0][0];
				matriz_g 	<= display_buffer[0][1];
				matriz_b 	<= display_buffer[0][2];
			end
			3'b001: begin
				matriz_col 	<= 8'b00000010;
				matriz_r 	<= display_buffer[1][0];
				matriz_g 	<= display_buffer[1][1];
				matriz_b 	<= display_buffer[1][2];
			end
			3'b010: begin
				matriz_col 	<= 8'b00000100;
				matriz_r 	<= display_buffer[2][0];
				matriz_g 	<= display_buffer[2][1];
				matriz_b 	<= display_buffer[2][2];
			end
			3'b011: begin
				matriz_col 	<= 8'b00001000;
				matriz_r 	<= display_buffer[3][0];
				matriz_g 	<= display_buffer[3][1];
				matriz_b 	<= display_buffer[3][2];
			end
			3'b100: begin
				matriz_col 	<= 8'b00010000;
				matriz_r 	<= display_buffer[4][0];
				matriz_g 	<= display_buffer[4][1];
				matriz_b 	<= display_buffer[4][2];
			end
			3'b101: begin
				matriz_col 	<= 8'b00100000;
				matriz_r 	<= display_buffer[5][0];
				matriz_g 	<= display_buffer[5][1];
				matriz_b 	<= display_buffer[5][2];
			end
			3'b110: begin
				matriz_col 	<= 8'b01000000;
				matriz_r 	<= display_buffer[6][0];
				matriz_g 	<= display_buffer[6][1];
				matriz_b 	<= display_buffer[6][2];
			end
			3'b111: begin
				matriz_col 	<= 8'b10000000;
				matriz_r 	<= display_buffer[7][0];
				matriz_g 	<= display_buffer[7][1];
				matriz_b 	<= display_buffer[7][2];
			end
		endcase
	
	end

	

endmodule
module contador_m #(parameter M=100, N=7)
  (
   input  wire          clock,
   input  wire          zera_as,
   input  wire          zera_s,
   input  wire          conta,
   output reg  [N-1:0]  Q,
   output reg           fim,
   output reg           meio    
  );

  always @(posedge clock or posedge zera_as) begin
    if (zera_as) begin
      Q <= 0;
    end else if (clock) begin
      if (zera_s) begin
        Q <= 0;
      end else if (conta) begin
        if (Q == M-1) begin
          Q <= 0;
        end else begin
          Q <= Q + 1'b1;
        end
      end
    end
  end

  // Saidas
  always @ (Q)
      if (Q == M-1)   fim = 1;
      else            fim = 0;

  always @ (Q)
      if (Q == M/2-1) meio = 1;
      else            meio = 0;

endmodule
*/
